# Fritzing sketch L293D_Motor_Driver_Schem (saved by Fritzing 0.9.3b)
breadboards: 1

parts:
  Part1 = Arduino Uno (Rev3)
  IC1 = L293D [package=THT]
  M1 = DC Motor
  M2 = DC Motor

nets:
  N1: Part1.D8, IC1.In_4
  N2: Part1.D9_PWM, IC1.In_3
  N3: Part1.D2, IC1.In_1
  N4: Part1.D3_PWM, IC1.In_2
  N5: Part1.5V, IC1.Enable_1, IC1.+Vmotor, IC1.Enable_2, IC1.+V
  GND: Part1.GND, IC1.0V, M1.pin_2, M2.pin_2
  N6: IC1.Out_1_(_Controlled_by_Enable_1_), IC1.Out_2_(_Controlled_by_Enable_1_), M1.pin_1
  N7: IC1.Out_3_(_Controlled_by_Enable_2_), IC1.Out_4_(_Controlled_by_Enable_2_), M2.pin_1
